# Fritzing sketch 3-1-2 (saved by Fritzing 1.0.6)
breadboards: 1

parts:
  U1 = SN74LS14N [package="DIP14 [THT]"]
  VCC1 = Battery [internal_resistance=0.1Ω]
  LED1 = smd LED [color="Red (633nm)" package="0603 [SMD]"]  # not connected

nets:
  N1: U1.1Y, U1.2A
  N2: U1.2Y, U1.3A
  N3: U1.3Y, U1.4A
  N4: U1.GND, VCC1.-
  N5: U1.4Y, U1.5A
  N6: U1.5Y, U1.6A
  N7: U1.VCC, VCC1.+
