// Logisim project 1_2_2.circ as structural Verilog: 1 circuit, main circuit main
module main (
  input  a,
  input  b,
  input  C_in,
  output S,
  output C_out
);

  wire and_1_out, and_2_out, xor_1_out;

  and and_1 (and_1_out, a, b);
  xor xor_1 (xor_1_out, a, b);
  xor xor_2 (S, xor_1_out, C_in);
  and and_2 (and_2_out, xor_1_out, C_in);
  or or_1 (C_out, and_2_out, and_1_out);

  // Notes on the sheet:
  //   a.b + C_in . (a xor b) = C_out
endmodule
