// Logisim project 2_2_2.circ as structural Verilog: 2 circuits, main circuit main
module main (
  input  C_in,
  input  b0,
  input  in_3,
  input  a0,
  input  in_5,
  input  in_6,
  input  b1,
  input  a1,
  input  in_9,
  input  in_10,
  input  b2,
  input  in_12,
  input  in_13,
  input  a2,
  input  in_15,
  input  in_16,
  input  b3,
  input  a3,
  output s0,
  output s1,
  output s2,
  output s3,
  output Overflow_Detector,
  output C_out
);

  wire and_1_out, and_2_out, and_3_out, and_4_out, and_5_out, and_6_out, and_7_out, and_8_out, c0, c1, c2,
       c3, C_out_t, full_adder_1_c_out, full_adder_2_c_out, full_adder_3_c_out, Overflow_Detector_t,
       xor_1_out, xor_2_out, xor_3_out, xor_4_out, xor_5_out, xor_6_out, xor_7_out, xor_8_out, xor_9_out,
       xor_10_out, xor_12_out;

  xor xor_1 (xor_1_out, C_in, b0);
  xor xor_2 (xor_2_out, C_in, b1);
  xor xor_3 (xor_3_out, C_in, b2);
  xor xor_4 (xor_4_out, C_in, b3);
  and and_1 (and_1_out, xor_1_out, a0);
  and and_2 (and_2_out, xor_2_out, a1);
  and and_3 (and_3_out, xor_3_out, a2);
  and and_4 (and_4_out, xor_4_out, a3);
  xor xor_5 (xor_5_out, xor_1_out, a0);
  xor xor_6 (xor_6_out, and_5_out, and_1_out);
  xor xor_7 (xor_7_out, xor_2_out, a1);
  xor xor_8 (xor_8_out, and_6_out, and_2_out);
  xor xor_9 (xor_9_out, xor_3_out, a2);
  xor xor_10 (xor_10_out, xor_4_out, a3);
  and and_5 (and_5_out, C_in, xor_5_out);
  xor xor_11 (s1, xor_6_out, xor_7_out);
  and and_6 (and_6_out, xor_6_out, xor_7_out);
  and and_7 (and_7_out, xor_8_out, xor_9_out);
  xor xor_12 (xor_12_out, and_7_out, and_3_out);
  and and_8 (and_8_out, xor_12_out, xor_10_out);
  xor xor_13 (s0, C_in, xor_5_out);
  xor xor_14 (s2, xor_8_out, xor_9_out);
  xor xor_15 (s3, xor_12_out, xor_10_out);
  xor xor_16 (C_out, and_8_out, and_4_out);
  xor xor_17 (Overflow_Detector, xor_12_out, C_out);
  Full_Adder full_adder_1 (.a(in_5), .b(in_6), .C_in(in_3), .S(c0), .C_out(full_adder_1_c_out));
  Full_Adder full_adder_2 (.a(in_9), .b(in_10), .C_in(full_adder_1_c_out), .S(c1), .C_out(full_adder_2_c_out));
  Full_Adder full_adder_3 (.a(in_12), .b(in_13), .C_in(full_adder_2_c_out), .S(c2), .C_out(full_adder_3_c_out));
  Full_Adder full_adder_4 (.a(in_15), .b(in_16), .C_in(full_adder_3_c_out), .S(c3), .C_out(C_out_t));
  xor xor_18 (Overflow_Detector_t, full_adder_3_c_out, C_out_t);

  // Notes on the sheet:
  //   C0
  //   C1
  //   C2
  //   C3
endmodule

// Full Adder
module Full_Adder (
  input  a,
  input  b,
  input  C_in,
  output S,
  output C_out
);

  wire and_1_out, and_2_out, xor_1_out;

  and and_1 (and_1_out, a, b);
  xor xor_1 (xor_1_out, a, b);
  xor xor_2 (S, xor_1_out, C_in);
  and and_2 (and_2_out, xor_1_out, C_in);
  or or_1 (C_out, and_2_out, and_1_out);
endmodule
