// Logisim project 2-1-1.circ as structural Verilog: 1 circuit, main circuit main
module main (
  input  Mode,
  input  D,
  input  C,
  input  B,
  input  A,
  input  S_in,
  output Q_D,
  output Q_C,
  output Q_B,
  output Q_A
);

  wire and_1_out, and_2_out, and_3_out, and_4_out, and_5_out, and_6_out, and_7_out, and_8_out, clock_1_out,
       not_1_out, or_1_out, or_2_out, or_3_out, or_4_out, undriven, undriven_2, undriven_3;

  not not_1 (not_1_out, Mode);
  and and_1 (and_1_out, D, Mode);
  and and_2 (and_2_out, undriven, not_1_out);
  and and_3 (and_3_out, C, Mode);
  and and_4 (and_4_out, undriven_2, not_1_out);
  and and_5 (and_5_out, B, Mode);
  and and_6 (and_6_out, undriven_3, not_1_out);
  and and_7 (and_7_out, A, Mode);
  and and_8 (and_8_out, S_in, not_1_out);
  or or_1 (or_1_out, and_1_out, and_2_out);
  or or_2 (or_2_out, and_3_out, and_4_out);
  or or_3 (or_3_out, and_5_out, and_6_out);
  or or_4 (or_4_out, and_7_out, and_8_out);
  Clock clock_1 (.out(clock_1_out));
  D_Flip_Flop d_ff_1 (.D(or_1_out), .clk(clock_1_out), .Q(Q_D));  // open: Qn, preset, reset
  D_Flip_Flop d_ff_2 (.D(or_2_out), .clk(clock_1_out), .Q(Q_C), .preset(undriven));  // open: Qn, reset
  D_Flip_Flop d_ff_3 (.D(or_3_out), .clk(clock_1_out), .Q(Q_B), .preset(undriven_2));  // open: Qn, reset
  D_Flip_Flop d_ff_4 (.D(or_4_out), .clk(clock_1_out), .Q(Q_A), .preset(undriven_3));  // open: Qn, reset
endmodule
