// Logisim project 2-2-1.circ as structural Verilog: 1 circuit, main circuit main
module main (
  input  A,
  input  B,
  input  C,
  input  D,
  input  Mode,
  input  S_in,
  output Q_A,
  output Q_B,
  output Q_C,
  output Q_D
);

  wire Clock_out;

  Shift_Register #(.length(4)) shift_register_1 (
    .in(S_in), .clk(Clock_out), .load(Mode), .d0(A), .q0(Q_A), .d1(B), .q1(Q_B), .d2(C), .q2(Q_C), .d3(D),
    .q3(Q_D));  // open: shift, out, clr
  Clock Clock (.out(Clock_out));
endmodule
