// Logisim project 2-2-2.circ as structural Verilog: 1 circuit, main circuit main
module main (
  input  A,
  input  B,
  input  C,
  input  D,
  input  Mode,
  input  S_in,
  output y,
  output Q_A,
  output Q_B,
  output Q_C,
  output Q_D
);

  wire and_1_out, and_2_out, and_3_out, and_4_out, Clock_out, not_1_out, not_2_out, not_3_out, not_4_out,
       not_5_out, not_6_out, not_7_out, not_8_out;

  Shift_Register #(.length(4)) shift_register_1 (
    .in(S_in), .clk(Clock_out), .load(Mode), .d0(A), .q0(Q_A), .d1(B), .q1(Q_B), .d2(C), .q2(Q_C), .d3(D),
    .q3(Q_D));  // open: shift, out, clr
  Clock Clock (.out(Clock_out));
  and and_1 (and_1_out, Q_A, Q_B, not_1_out, Q_D);
  not not_1 (not_1_out, Q_C);
  and and_2 (and_2_out, Q_A, Q_B, Q_C, not_2_out);
  not not_2 (not_2_out, Q_D);
  not not_3 (not_3_out, Q_A);
  not not_4 (not_4_out, Q_B);
  and and_3 (and_3_out, not_3_out, not_4_out, Q_C, not_5_out);
  not not_5 (not_5_out, Q_D);
  not not_6 (not_6_out, Q_A);
  not not_7 (not_7_out, Q_B);
  and and_4 (and_4_out, not_6_out, not_7_out, not_8_out, Q_D);
  not not_8 (not_8_out, Q_C);
  or or_1 (y, and_1_out, and_2_out, and_3_out, and_4_out);
endmodule
